# Fritzing sketch Skematik Fritzing (saved by Fritzing 0.9.3b)

parts:
  Part1 = Arduino Uno (Rev3)
  GY1 = GY-521 (MPU-6050) [form="♀ (female)" package=THT]
  S1 = H-Bridge with L298N
  M2 = DC Motor
  M3 = DC Motor
  VCC1 = Battery
  D1 = P1000K [part_number=P1000K]
  U1 = SWITCH-SPST-2 [package=switch-spst-vertical]

nets:
  N1: Part1.A4/SDA, GY1.pin4
  N2: Part1.A5/SCL, GY1.pin3
  N3: Part1.D8, S1.IN3
  N4: Part1.D9_PWM, S1.IN4
  N5: Part1.D10_PWM/SS, S1.ENB
  N6: Part1.D2, GY1.pin8
  N7: Part1.D5_PWM, S1.ENA
  N8: Part1.D6_PWM, S1.IN1
  N9: Part1.D7, S1.IN2
  N10: Part1.3V3, GY1.pin1
  5V: Part1.5V, S1.5V
  GND: Part1.GND, GY1.pin2, S1.GND, VCC1.-
  N11: S1.12V, D1.cathode
  N12: S1.M1-01, M3.pin_2
  N13: S1.M1-02, M3.pin_1
  N14: S1.M2-01, M2.pin_2
  N15: S1.M2-02, M2.pin_1
  N16: VCC1.+, U1.O
  N17: D1.anode, U1.P

custom parts:
  GY-521 (MPU-6050): Placa GY-521 basada en conjunto de acelerómetro+giroscopios MPU-6050
  H-Bridge with L298N: h-bridge
  Battery: Your standard 2x 18650 battery pack (7,4 Volts)
